// Logisim project ECU.circ as structural Verilog: 6 circuits, main circuit main
module main (
);

  wire [7:0] register_1_q, register_2_q, rpmcalculator_1_rpm_register;

  RPMCalculator rpmcalculator_1 (.RPM_Register(rpmcalculator_1_rpm_register));  // open: Hall_Sense, System_CIN, Output_Enable
  Bus_Transciever bus_transciever_1 (.S_IN(register_1_q), .S_OUT(rpmcalculator_1_rpm_register));  // open: Oen
  Register register_1 (.D(rpmcalculator_1_rpm_register), .Q(register_1_q));  // open: en, clk, clr
  Bus_Transciever bus_transciever_2 (.S_IN(register_2_q), .S_OUT(rpmcalculator_1_rpm_register));  // open: Oen
  Register register_2 (.D(rpmcalculator_1_rpm_register), .Q(register_2_q));  // open: en, clk, clr
endmodule

module RPMCalculator (
  input  Hall_Sense,
  input  System_CIN,
  output [7:0] RPM_Register,
  output Output_Enable
);

  wire carry, n74193_1_pin4, n74193_1_pin12, n74193_2_pin4, n74193_3_pin4, not_1_out;
  wire [7:0] n74193_2_pin3, n74245_1_pin2;

  _74245 #(.ShowInternalStructure("true")) u_74245_1 (
    .pin1(Output_Enable), .pin2(n74245_1_pin2[0]), .pin3(n74245_1_pin2[1]), .pin4(n74245_1_pin2[2]),
    .pin5(n74245_1_pin2[3]), .pin6(n74245_1_pin2[4]), .pin7(n74245_1_pin2[5]), .pin8(n74245_1_pin2[6]),
    .pin9(n74245_1_pin2[7]), .pin18(RPM_Register[0]), .pin17(RPM_Register[1]), .pin16(RPM_Register[2]),
    .pin15(RPM_Register[3]), .pin14(RPM_Register[4]), .pin13(RPM_Register[5]), .pin12(RPM_Register[6]),
    .pin11(RPM_Register[7]));  // open: pin19
  Register register_1 (.D(n74193_2_pin3), .en(not_1_out), .clk(not_1_out), .Q(n74245_1_pin2));  // open: clr
  not not_1 (not_1_out, n74193_1_pin12);
  _74193 #(.ShowInternalStructure("true")) u_74193_1 (
    .pin4(n74193_1_pin4), .pin5(System_CIN), .pin12(n74193_1_pin12));  // open: pin1, pin2, pin3, pin6, pin7, pin15, pin14, pin13, pin11, pin10, pin9
  _74193 #(.ShowInternalStructure("true")) u_74193_2 (
    .pin2(n74193_2_pin3[1]), .pin3(n74193_2_pin3[0]), .pin4(n74193_2_pin4), .pin5(Hall_Sense),
    .pin6(n74193_2_pin3[2]), .pin7(n74193_2_pin3[3]), .pin14(not_1_out), .pin12(carry));  // open: pin1, pin15, pin13, pin11, pin10, pin9
  _74193 #(.ShowInternalStructure("true")) u_74193_3 (
    .pin2(n74193_2_pin3[5]), .pin3(n74193_2_pin3[4]), .pin4(n74193_3_pin4), .pin5(carry),
    .pin6(n74193_2_pin3[6]), .pin7(n74193_2_pin3[7]), .pin14(not_1_out));  // open: pin1, pin15, pin13, pin12, pin11, pin10, pin9
  // also tied to VCC on the sheet: {n74193_1_pin4, n74193_2_pin4, n74193_3_pin4}

  // Notes on the sheet:
  //   Output_Enable: pull=down
endmodule

module Bus_Transciever (
  input  Oen,
  input  [7:0] S_IN,
  output [7:0] S_OUT
);

  _74245 #(.ShowInternalStructure("true")) u_74245_1 (
    .pin1(Oen), .pin2(S_IN[0]), .pin3(S_IN[1]), .pin4(S_IN[2]), .pin5(S_IN[3]), .pin6(S_IN[4]),
    .pin7(S_IN[5]), .pin8(S_IN[6]), .pin9(S_IN[7]), .pin18(S_OUT[0]), .pin17(S_OUT[1]), .pin16(S_OUT[2]),
    .pin15(S_OUT[3]), .pin14(S_OUT[4]), .pin13(S_OUT[5]), .pin12(S_OUT[6]), .pin11(S_OUT[7]));  // open: pin19

  // Notes on the sheet:
  //   Oen: pull=down
endmodule

module Control_Logic (
  input  CIN,
  output [7:0] out_2
);

  wire n74193_1_pin4, n74193_1_pin5, n74193_2_pin4, not_1_out;
  wire [7:0] n74193_2_pin3, rom_1_data;

  _74193 #(.ShowInternalStructure("true")) u_74193_1 (
    .pin2(n74193_2_pin3[5]), .pin3(n74193_2_pin3[4]), .pin4(n74193_1_pin4), .pin5(n74193_1_pin5),
    .pin6(n74193_2_pin3[6]), .pin7(n74193_2_pin3[7]));  // open: pin1, pin15, pin14, pin13, pin12, pin11, pin10, pin9
  _74193 #(.ShowInternalStructure("true")) u_74193_2 (
    .pin2(n74193_2_pin3[1]), .pin3(n74193_2_pin3[0]), .pin4(n74193_2_pin4), .pin5(CIN),
    .pin6(n74193_2_pin3[2]), .pin7(n74193_2_pin3[3]), .pin12(n74193_1_pin5));  // open: pin1, pin15, pin14, pin13, pin11, pin10, pin9
  ROM rom_1 (.addr(n74193_2_pin3), .data(rom_1_data));
  not not_1 (not_1_out, CIN);
  Register register_1 (.D(rom_1_data), .en(not_1_out), .clk(not_1_out), .Q(out_2));  // open: clr
  // also tied to VCC on the sheet: {n74193_1_pin4, n74193_2_pin4}

  // Notes on the sheet:
  //   contents of rom_1 (hex, n*v repeats v):
  //   1 2 3 4
endmodule

module RPM_TESTING (
  output [7:0] RPM_Register
);

  wire carry, n74193_1_pin4, n74193_1_pin5, n74193_1_pin12, n74193_2_pin4, n74193_2_pin5, n74193_3_pin4,
       n74245_1_pin1, not_1_out;
  wire [7:0] n74193_2_pin3, n74245_1_pin2;

  _74245 #(.ShowInternalStructure("true")) u_74245_1 (
    .pin1(n74245_1_pin1), .pin2(n74245_1_pin2[0]), .pin3(n74245_1_pin2[1]), .pin4(n74245_1_pin2[2]),
    .pin5(n74245_1_pin2[3]), .pin6(n74245_1_pin2[4]), .pin7(n74245_1_pin2[5]), .pin8(n74245_1_pin2[6]),
    .pin9(n74245_1_pin2[7]), .pin18(RPM_Register[0]), .pin17(RPM_Register[1]), .pin16(RPM_Register[2]),
    .pin15(RPM_Register[3]), .pin14(RPM_Register[4]), .pin13(RPM_Register[5]), .pin12(RPM_Register[6]),
    .pin11(RPM_Register[7]));  // open: pin19
  Button button_1 (.out(n74245_1_pin1));
  Register register_1 (.D(n74193_2_pin3), .en(not_1_out), .clk(not_1_out), .Q(n74245_1_pin2));  // open: clr
  not not_1 (not_1_out, n74193_1_pin12);
  _74193 #(.ShowInternalStructure("true")) u_74193_1 (
    .pin4(n74193_1_pin4), .pin5(n74193_1_pin5), .pin12(n74193_1_pin12));  // open: pin1, pin2, pin3, pin6, pin7, pin15, pin14, pin13, pin11, pin10, pin9
  _74193 #(.ShowInternalStructure("true")) u_74193_2 (
    .pin2(n74193_2_pin3[1]), .pin3(n74193_2_pin3[0]), .pin4(n74193_2_pin4), .pin5(n74193_2_pin5),
    .pin6(n74193_2_pin3[2]), .pin7(n74193_2_pin3[3]), .pin14(not_1_out), .pin12(carry));  // open: pin1, pin15, pin13, pin11, pin10, pin9
  _74193 #(.ShowInternalStructure("true")) u_74193_3 (
    .pin2(n74193_2_pin3[5]), .pin3(n74193_2_pin3[4]), .pin4(n74193_3_pin4), .pin5(carry),
    .pin6(n74193_2_pin3[6]), .pin7(n74193_2_pin3[7]), .pin14(not_1_out));  // open: pin1, pin15, pin13, pin12, pin11, pin10, pin9
  Clock clock_1 (.out(n74193_1_pin5));
  Button button_2 (.out(n74193_2_pin5));
  // also tied to VCC on the sheet: {n74193_1_pin4, n74193_2_pin4, n74193_3_pin4}
endmodule

module Control_Logic_TESTING (
);

  wire n74193_1_pin4, n74193_1_pin5, n74193_2_pin4, n74193_2_pin5, not_1_out;
  wire [7:0] n74193_2_pin3, rom_1_data;

  _74193 #(.ShowInternalStructure("true")) u_74193_1 (
    .pin2(n74193_2_pin3[5]), .pin3(n74193_2_pin3[4]), .pin4(n74193_1_pin4), .pin5(n74193_1_pin5),
    .pin6(n74193_2_pin3[6]), .pin7(n74193_2_pin3[7]));  // open: pin1, pin15, pin14, pin13, pin12, pin11, pin10, pin9
  _74193 #(.ShowInternalStructure("true")) u_74193_2 (
    .pin2(n74193_2_pin3[1]), .pin3(n74193_2_pin3[0]), .pin4(n74193_2_pin4), .pin5(n74193_2_pin5),
    .pin6(n74193_2_pin3[2]), .pin7(n74193_2_pin3[3]), .pin12(n74193_1_pin5));  // open: pin1, pin15, pin14, pin13, pin11, pin10, pin9
  ROM rom_1 (.addr(n74193_2_pin3), .data(rom_1_data));
  Clock clock_1 (.out(n74193_2_pin5));
  not not_1 (not_1_out, n74193_2_pin5);
  Register register_1 (.D(rom_1_data), .en(not_1_out), .clk(not_1_out));  // open: Q, clr
  // also tied to VCC on the sheet: {n74193_1_pin4, n74193_2_pin4}

  // Notes on the sheet:
  //   contents of rom_1 (hex, n*v repeats v):
  //   1 2 3 4
endmodule
